// Digital circuit Templatet.dig as structural Verilog
module Templatet (
  input  [3:0] In,
  input  [1:0] Selector,
  output [7:0] Output
);

  wire i0b, i1b, i2b, i3b, s0b;

  not not_1 (i0b, In[0]);
  not not_2 (s0b, Selector[0]);
  not not_3 (i1b, In[1]);
  not not_4 (Selector[1], Selector[1]);
  not not_5 (i2b, In[2]);
  not not_6 (i3b, In[3]);
  // Pins of 4 and 8 bits meet at Output

  // Other names for the same wires on the sheet: i0 = In[0]; i1 = In[1]; i2 = In[2]; i3 = In[3]; s0 = Selector[0];
  //   s1 = Selector[1]
endmodule
